# Fritzing sketch schematic (saved by Fritzing 0.9.3b)
breadboards: 1

parts:
  Part1 = Arduino Pro Mini v13
  S1 = Round Pushbutton
  VCC1 = Battery
  S2 = Round Pushbutton
  R1 = Resistor [tolerance=±5% resistance=30k package=THT]
  LED1 = LED - 3mm [color="Red (633nm)" package="3 mm [THT]"]
  R2 = Resistor [tolerance=±5% resistance=30k package=THT]
  microSD1 = MicroSD Card Module
  JP1 = Header 8 [package=1x08_smd]

nets:
  N1: Part1.RAW, S1.leg1, microSD1.VCC
  GND: Part1.GND, VCC1.-, S2.leg1, LED1.cathode, microSD1.GND, JP1.2
  N2: Part1.D13/SCK, microSD1.SCK, JP1.4
  N3: Part1.D12/MISO, microSD1.MISO
  N4: Part1.D11_PWM/MOSI, microSD1.MOSI, JP1.3
  N5: Part1.D10_PWM/SS, JP1.5
  N6: Part1.D9_PWM, JP1.6
  N7: Part1.D8, JP1.7
  N8: Part1.D7, JP1.8
  N9: Part1.D6_PWM, microSD1.CS
  N10: Part1.D5_PWM, S2.leg0, R1.Pin_1
  N11: Part1.D4, R2.Pin_0
  N12: S1.leg0, VCC1.+
  N13: R1.Pin_0, JP1.1
  N14: LED1.anode, R2.Pin_1

notes:
  e-Paper
  Arduino (3.3V)
  3.3V
  3V3
  GND
  GND
  DIN
  D11
  CLK
  D13
  CS
  D10
  DC
  D9
  RST
  D8
  BUSY
  D7
